# Fritzing sketch mcr breadboard v2 WIP (saved by Fritzing 0.9.3b)
circuit board: 8.46667cm x 5.64444cm
breadboards: 1

parts:
  Part2 = Adafruit TCA9548A
  R1 = Resistor [tolerance=±5% resistance=2.2 package=THT]
  R2 = Resistor [tolerance=±5% resistance=2.2 package=THT]
  Part1 = Adafruit HUZZAH32 ESP32 Feather [part_number="Adafruit #3405"]
  Part3 = HTU21D-F Temperature + Humidity Sensor
  R3 = Resistor [tolerance=±5% resistance=2.2 package=THT]
  R4 = Resistor [tolerance=±5% resistance=2.2 package=THT]
  J1 = Screw terminal - 2 pins [package=THT]
  J2 = Screw terminal - 2 pins [package=THT]
  J3 = Screw terminal - 2 pins [package=THT]
  J4 = screw terminal, 4 pins

nets:
  N1: Part2.7SDA, Part3.SDA
  N2: Part2.7SCL, Part3.SCL
  VCC: Part2.VCC, Part2.RESET, R1.Pin_1, R2.Pin_1, Part1.3.3V, Part3.VIN, R3.Pin_1, R4.Pin_1, J1.pin2, J3.pin2
  GND: Part2.GND, Part1.GND, Part3.GND, J1.pin1, J3.pin1
  N3: Part2.INPUTSDA, Part1.SDA
  N4: Part2.INPUTSCL, Part1.SCL
  N5: Part2.0SDA, R1.Pin_0, J2.pin1
  N6: Part2.0SCL, R2.Pin_0, J2.pin2
  N7: Part2.1SDA, R3.Pin_0, J4.pin1
  N8: Part2.1SCL, R4.Pin_0, J4.pin2

custom parts:
  Adafruit TCA9548A: You just found the perfect I2C sensor, and you want to wire up two or three or more of them to your Arduino when you realize "Uh oh, this chip has a fixed I2C address, and from what I know about I2C, you cannot have two devices with the same address on the same SDA/SCL pins!" Are you out of luck? You would be, if you didn't have this ultra-cool TCA9548A 1-to-8 I2C multiplexer! Finally, a way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
  HTU21D-F Temperature + Humidity Sensor: This I2C digital humidity sensor is an accurate and intelligent alternative to the much simpler Humidity and Temperature Sensor - SHT15 Breakout It has a typical accuracy of ±2% with an operating range that's optimized from 5% to 95% RH. Operation outside this range is still possible - just the accuracy might drop a bit. The temperature output has an accuracy of ±1°C from -30~90°C. If you're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
